# Fritzing sketch WLANPump (saved by Fritzing 0.9.7b)
breadboards: 1

parts:
  ESP8266 = SparkFun ESP8266 Thing
  Soil_Sensor = Soil Moisture Sensor
  Power_plug1 = Power plug
  Water_Tank_Sensor = Soil Moisture Sensor
  Signal_LED = LED - 3mm [color="Red (633nm)" package="3 mm [THT]"]
  R1 = Resistor [tolerance=±5% resistance=220 package="2010 [SMD]"]
  Pump_Relay = RELAY [package=relay-jzc]
  Pump_Output = Power plug

nets (from the schematic view):
  GND: ESP8266.GND, Soil_Sensor.GND, Power_plug1.GND, Water_Tank_Sensor.GND, Signal_LED.anode, Pump_Relay.NO, Pump_Relay.COIL1
  N1: ESP8266.GPIO2, Water_Tank_Sensor.SIG
  VCC: ESP8266.VIN, Soil_Sensor.VCC, Power_plug1.VCC, Water_Tank_Sensor.VCC, Pump_Output.VCC
  N2: ESP8266.GPIO5, R1.Pin_0
  N3: ESP8266.GPIO13, Pump_Relay.COIL2
  N4: ESP8266.ADC, Soil_Sensor.SIG
  N5: Signal_LED.cathode, R1.Pin_1
  N6: Pump_Relay.MAIN, Pump_Output.GND
